# Fritzing sketch circuit (saved by Fritzing 0.9.3b)
circuit board: 10cm x 10cm
breadboards: 2

parts:
  Teensy1 = Teensy 3.6 (Basic)
  IC2 = DIP - 40 pins [chip_label=W65C02 package="DIP (Dual Inline) [THT]"]

nets:
  GND: Teensy1.GND, Teensy1.GND1, IC2.VSS
  N1: Teensy1.D13, IC2.A10
  N2: Teensy1.A0/D14, IC2.A9
  N3: Teensy1.A1/D15, IC2.A8
  N4: Teensy1.A2/D16, IC2.A7
  N5: Teensy1.A3/D17, IC2.A6
  N6: Teensy1.A4/D18, IC2.A5
  N7: Teensy1.A5/D19, IC2.A4
  N8: Teensy1.A6/D20, IC2.A3
  N9: Teensy1.A7/D21, IC2.A2
  N10: Teensy1.A8/D22, IC2.A1
  N11: Teensy1.A9/D23, IC2.A0
  3V3: Teensy1.3V3, Teensy1.3V3_1, IC2.RDY, IC2.IRQB, IC2.NMIB, IC2.VDD, IC2.BE, IC2.SOB
  N12: Teensy1.D24, IC2.RESB
  N13: Teensy1.D25, IC2.D0
  N14: Teensy1.D26, IC2.D1
  N15: Teensy1.D27, IC2.D2
  N16: Teensy1.D28, IC2.D3
  N17: Teensy1.D29, IC2.D4
  N18: Teensy1.D30, IC2.D5
  N19: Teensy1.D31, IC2.D6
  N20: Teensy1.D32, IC2.D7
  N21: Teensy1.D33, IC2.PHI2
  N22: Teensy1.D34, IC2.RWB
  N23: Teensy1.D35, IC2.A15
  N24: Teensy1.D36, IC2.A14
  N25: Teensy1.D37, IC2.A13
  N26: Teensy1.D38, IC2.A12
  N27: Teensy1.D39, IC2.A11

custom parts:
  Teensy 3.6 (Basic): The Teensy is a complete USB-based microcontoller development system, in a very small footprint, capable of implementing many types of projects. All programming is done via the USB port. No special programmer is needed, only a standard micro-USB cable and a PC or Macintosh with a USB port.
  DIP - 40 pins: A DIP stand-in part for whatever IC you want. With 40 pins on a 300mil dual inline package (DIP) footprint.
